# Fritzing sketch commonAnodeRGBLED (saved by Fritzing 0.9.2b)

parts:
  부품1 = Bluetooth HC-06
  LED1 = RGB LED - (4 legs) [package="5 mm [THT]"]
  부품2 = Arduino Uno (Rev3) - ICSP
  부품3 = Arduino Nano (Rev3.0)
  LED2 = RGB LED - (4 legs) [package="5 mm [THT]"]
  부품4 = Bluetooth HC-06

nets:
  N1: 부품1.RXD, 부품2.D0/RX
  N2: 부품1.TXD, 부품2.D1/TX
  GND: 부품1.GND, 부품2.GND
  VCC: 부품1.VCC, 부품2.5V
  N3: LED1.red_cathode, 부품2.D9_PWM
  N4: LED1.common_anode, 부품2.D6_PWM
  N5: LED1.green_cathode, 부품2.D10_PWM/SS
  N6: LED1.blue_cathode, 부품2.D11_PWM/MOSI
  N7: 부품3.D1/TX, 부품4.RXD
  N8: 부품3.D0/RX, 부품4.TXD
  GND_2: 부품3.GND, 부품4.GND
  N9: 부품3.D6, LED2.common_anode
  N10: 부품3.D9, LED2.red_cathode
  N11: 부품3.D10, LED2.green_cathode
  N12: 부품3.D11/MOSI, LED2.blue_cathode
  5V: 부품3.5V, 부품4.VCC
