# Fritzing sketch neo pixel(bar) (saved by Fritzing 0.9.3b)
breadboards: 1

parts:
  부품1 = Arduino Uno (Rev3)
  BT1 = Bluetooth HC-06u [package=THT]
  부품2 = NeoPixel Stick [part_number=1426]

nets:
  N1: 부품1.D0/RX, BT1.TXD
  N2: 부품1.D1/TX, BT1.RXD
  N3: 부품1.D6_PWM, 부품2.DATAIN
  5V: 부품1.5V, BT1.VCC, 부품2.+5V
  GND: 부품1.GND, BT1.GND, 부품2.GND

custom parts:
  Bluetooth HC-06u: Bluetooth HC-06 - face up, pins down 16.5mm x 37.5mm PCB
  NeoPixel Stick: Make your own little LED strip arrangement with this stick of NeoPixel LEDs. We crammed 8 of the tiny 5050 (5mm x 5mm) smart RGB LEDs onto a PCB with mounting holes and a chainable design. Use only one microcontroller pin to control as many as you can chain together! Each LED is addressable as the driver chip is inside the LED. Each one has ~18mA constant current drive so the color will be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
