# Fritzing sketch neo pixel(jewel) (saved by Fritzing 0.9.2b)
breadboards: 1

parts:
  부품1 = Arduino Uno (Rev3)
  BT1 = Bluetooth HC-06u [package=THT]
  부품3 = NeoPixel Jewel

nets:
  N1: 부품1.D0/RX, BT1.TXD
  N2: 부품1.D1/TX, BT1.RXD
  N3: 부품1.D6_PWM, 부품3.Data_In
  5V: 부품1.5V, BT1.VCC, 부품3.VDD
  GND: 부품1.GND, BT1.GND, 부품3.GND

custom parts:
  Bluetooth HC-06u: Bluetooth HC-06 - face up, pins down 16.5mm x 37.5mm PCB
  NeoPixel Jewel: Seven of our the tiny 5050 (5mm x 5mm) smart RGB LEDs onto a beautiful, round PCB with mounting holes and a chainable design to create what we think is our most elegant (and evening-wear appropriate) NeoPixel board yet.
